# Fritzing sketch schema (saved by Fritzing 0.9.2b)

parts:
  U1 = Breadboard Power Supply [package=THT]
  U2 = NodeMCU V3.0
  Composant1 = SRF05 Ultrasonic Rangefinder

nets:
  N1: U1.pin2, U2.GND
  N2: U1.pin4, U2.3V3
  N3: U1.pin6, Composant1.connector11
  N4: U1.pin8, Composant1.connector8
  N5: U2.D0, U2.RST
  N6: U2.D1, Composant1.connector9
  N7: U2.D2, Composant1.connector10

custom parts:
  Breadboard Power Supply: Représentation Carte Breadboard Power Supply
  NodeMCU V3.0: ESP8266 based NodeMCU
